# Fritzing sketch R2R_ladder-000-aa (saved by Fritzing 0.9.0b)
breadboards: 1

parts:
  VCC1 = Battery
  S1 = Pushbutton [package="[THT]"]
  R1 = Resistor [tolerance=±5% resistance=100k package=THT]
  R2 = Resistor [tolerance=±5% resistance=100k package=THT]
  R3 = Resistor [tolerance=±5% resistance=47k package=THT]
  R4 = Resistor [tolerance=±5% resistance=100k package=THT]
  S2 = Pushbutton [package="[THT]"]
  R5 = Resistor [tolerance=±5% resistance=47k package=THT]
  R6 = Resistor [tolerance=±5% resistance=100k package=THT]
  S3 = Pushbutton [package="[THT]"]
  R7 = Resistor [tolerance=±5% resistance=47k package=THT]
  S4 = Pushbutton [package="[THT]"]
  R8 = Resistor [tolerance=±5% resistance=100k package=THT]
  R9 = Resistor [tolerance=±5% resistance=47k package=THT]
  S5 = Pushbutton [package="[THT]"]
  S6 = Pushbutton [package="[THT]"]
  S7 = Pushbutton [package="[THT]"]
  S8 = Pushbutton [package="[THT]"]
  R10 = Resistor [tolerance=±5% resistance=100k package=THT]
  R11 = Resistor [tolerance=±5% resistance=47k package=THT]
  R12 = Resistor [tolerance=±5% resistance=100k package=THT]
  R13 = Resistor [tolerance=±5% resistance=47k package=THT]
  R14 = Resistor [tolerance=±5% resistance=100k package=THT]
  R15 = Resistor [tolerance=±5% resistance=47k package=THT]
  R16 = Resistor [tolerance=±5% resistance=100k package=THT]
  LED1 = LED - 5mm [color="Red (633nm)" package="5 mm [THT]"]

nets:
  N1: VCC1.-, R1.Pin_1, LED1.cathode
  N2: VCC1.+, S1.Pin_3, S1.Pin_4, S2.Pin_3, S2.Pin_4, S3.Pin_3, S3.Pin_4, S4.Pin_3, S4.Pin_4, S5.Pin_3, S5.Pin_4, S6.Pin_3, S6.Pin_4, S7.Pin_3, S7.Pin_4, S8.Pin_3, S8.Pin_4
  N3: S1.Pin_1, S1.Pin_2, R2.Pin_1
  N4: R1.Pin_0, R2.Pin_0, R3.Pin_1
  N5: R3.Pin_0, R4.Pin_0, R5.Pin_1
  N6: R4.Pin_1, S2.Pin_1, S2.Pin_2
  N7: R5.Pin_0, R6.Pin_0, R7.Pin_1
  N8: R6.Pin_1, S3.Pin_1, S3.Pin_2
  N9: R7.Pin_0, R8.Pin_0, R9.Pin_1
  N10: S4.Pin_1, S4.Pin_2, R8.Pin_1
  N11: R9.Pin_0, R10.Pin_0, R11.Pin_1
  N12: S5.Pin_1, S5.Pin_2, R10.Pin_1
  N13: S6.Pin_1, S6.Pin_2, R12.Pin_1
  N14: S7.Pin_1, S7.Pin_2, R14.Pin_1
  N15: S8.Pin_1, S8.Pin_2, R16.Pin_1
  N16: R11.Pin_0, R12.Pin_0, R13.Pin_1
  N17: R13.Pin_0, R14.Pin_0, R15.Pin_1
  N18: R15.Pin_0, R16.Pin_0, LED1.anode

notes:
  The LED is there to mark the circuit's output, only.
  It is not normally present in the operational circuit.
  Instead, connect the ADC input pin where the LED
  anode is shown to be connected (jcn R15 and R16)
